# Fritzing sketch blinky555 (saved by Fritzing 0.7.12b)
breadboards: 1

parts:
  U1 = 555 Timer [package="DIP8 [THT]"]
  R1 = Resistor [tolerance=±5% resistance=220 package=THT]

nets:
  N1: U1.Trigger, R1.Pin_1
  N2: U1.Discharge, R1.Pin_0
